# Fritzing sketch lcd_display (saved by Fritzing 0.9.2b)
breadboards: 1

parts:
  U1 = LCD-16X2 [package=lcd-16x2]
  Part1 = Arduino Uno (Rev3) - ICSP
  R1 = Rotary Potentiometer (Small) [maximum_resistance=100kΩ package=THT]

nets:
  VSS: U1.VSS, U1.R_W, U1.K, Part1.GND, R1.leg1
  VDD: U1.VDD, U1.A, Part1.5V
  N1: U1.VO, R1.wiper
  N2: U1.RS, Part1.D7
  N3: U1.E, Part1.D8
  N4: U1.DB4, Part1.D9_PWM
  N5: U1.DB5, Part1.D10_PWM/SS
  N6: U1.DB6, Part1.D11_PWM/MOSI
  N7: U1.DB7, Part1.D12/MISO

notes:
  LCD Display
  Thejesh GN
  Connections:
  * STEP 0. SETUP BREADBOARD
  Arduino 5v (pin 3) -> plus column on breadboard
  Arduino GND (pin 4 or 5) -> min column on breadboard
  * STEP 1. POWER UP
  Connect: GND row (min) on breadboard > pin 1 on LCD (VSS)
  Connect: +5v row (plus) on breadboard > pin 2 on LCD (VDD)
  Connect: +5v row (plus) on breadboard > pin 15 on LCD (A)
  Connect: GND row (min) on breadboard > pin 16 on LCD (K)
  Now connect Arduino to power, LCD should light up and show boxes
  * STEP 2. POT FOR CONTRAST
  Connect: 1st pin of the pot > GND (min) of the breadboard
  Connect: 2nd pin of the pot > pin 3 of the LCD display (VO)
  Connect: 3rd pin of the pot > +5v (plus) of bread board
  Now by changing the pot value you should be able to change the contrast
  * STEP 3. CONNECT DATA Lines
  Connect: pin 4 of the LCD display (RS) > pin 7 of the Arduino (PWM)
  Connect: pin 5 of the LCD display (RW) > GND row of the breadboard
  Connect: pin 6 of the LCD display (E) > pin 8 of the Arduino (PWM)
  Connect: pin 11 of the LCD display (D4) > pin 9 of the Arduino (PWM)
  Connect: pin 12 of the LCD display (D5) > pin 10 of the Arduino (PWM)
  Connect: pin 13 of the LCD display (D6) > pin 11 of the Arduino (PWM)
  Connect: pin 14 of the LCD display (D7) > pin 12 of the Arduino (PWM)
